// Logisim project carry_generator.circ as structural Verilog: 1 circuit, main circuit main
module main (
  input  c0_in,
  input  p0,
  input  g0,
  input  p1,
  input  g1,
  input  p2,
  input  g2,
  input  p3,
  input  g3,
  output c0_out,
  output c1,
  output c2,
  output c3,
  output c4
);

  wire and_1_out, and_2_out, and_4_out, and_5_out, and_6_out, and_7_out, and_8_out, and_9_out, and_10_out,
       and_11_out;

  and and_1 (and_1_out, c0_in, p0);
  and and_2 (and_2_out, g0, p1);
  // AND_Gate and_3 has open pins: in0=p1, in1=p2, out=open
  and and_4 (and_4_out, g1, p2);
  and and_5 (and_5_out, g2, p3);
  and and_6 (and_6_out, and_1_out, p1);
  and and_7 (and_7_out, and_1_out, and_4_out);
  and and_8 (and_8_out, and_2_out, p2);
  and and_9 (and_9_out, and_4_out, p3);
  and and_10 (and_10_out, and_7_out, p3);
  and and_11 (and_11_out, p3, and_8_out);
  or or_1 (c1, and_1_out, g0);
  or or_2 (c2, and_6_out, and_2_out, g1);
  or or_3 (c3, and_7_out, and_8_out, and_4_out, g2);
  or or_4 (c4, and_9_out, and_10_out, and_5_out, and_11_out, g3);

  assign c0_out = c0_in;
endmodule
